# Fritzing sketch Count_Down_Launcher (saved by Fritzing 0.9.2b)

parts:
  Part1 = Arduino Uno (Rev3)
  R1 = Resistor [tolerance=±5% resistance=10k package=THT]
  S3 = Relay [part_number=RELAY package=THT]
  M1 = DC Motor
  Vcc = Battery
  S2 = Momentary Switch [package=ksa_sealed_tac_switch]
  S1 = SWITCH_SPDT [package=kps-1290]
  R2 = Resistor [tolerance=±5% resistance=100 package=THT]
  LED1 = LED - 5mm [color="Red (633nm)" package="5 mm [THT]"]
  LED2 = LED - 5mm [color="Green (565nm)" package="5 mm [THT]"]

nets:
  N1: Part1.GND, R1.Pin_1, S3.COIL1
  N2: Part1.D2, S3.COIL2
  N3: Part1.D3_PWM, R1.Pin_0, S2.1
  N4: Part1.D4, LED1.cathode
  N5: Part1.D5_PWM, LED2.cathode
  N6: Part1.3V3, S2.3
  N7: Part1.5V, R2.Pin_1
  N8: S3.A, S1.O
  N9: S3.B, M1.pin_2
  N10: M1.pin_1, Vcc.+
  N11: Vcc.-, S1.P
  N12: R2.Pin_0, LED1.anode, LED2.anode
