# Fritzing sketch Internet_LED (saved by Fritzing 0.9.2b)

parts:
  R1 = Resistor [tolerance=±5% resistance=100 package="1206 [SMD]"]
  D1 = LEDs [package=led10mm]
  Photon = Photon

nets:
  N1: R1.Pin_0, Photon.D2
  N2: R1.Pin_1, D1.C
  N3: D1.A, Photon.3V3
