# Fritzing sketch Internet_Music (saved by Fritzing 0.9.2b)

parts:
  R1 = Resistor [tolerance=±5% resistance=100 package="1206 [SMD]"]
  D1 = LEDs [package=led10mm]
  Photon = Photon
  SP1 = SPEAKER [package=pcb_mount_speaker]
  U1 = IC, SIP package, 5 pins [chip_label="Music IC"]

nets:
  N1: R1.Pin_0, U1.pin5
  N2: R1.Pin_1, SP1.-
  N3: D1.A, Photon.D2, U1.pin2
  N4: D1.C, Photon.GND, U1.pin1
  N5: Photon.D3, U1.pin4
  N6: Photon.3V3, SP1.+, U1.pin3
