# Fritzing sketch Internet_Sounds (saved by Fritzing 0.9.2b)

parts:
  Photon = Photon
  SP1 = SPEAKER [package=pcb_mount_speaker]
  U2 = IC, SIP package, 5 pins [chip_label="Alarm IC"]

nets:
  N1: Photon.GND, U2.pin1
  N2: Photon.D2, U2.pin2
  N3: Photon.D3, U2.pin3
  N4: Photon.D4, U2.pin4
  N5: Photon.3V3, SP1.-
  N6: SP1.+, U2.pin5
