# Fritzing sketch Measuring_Light (saved by Fritzing 0.9.2b)

parts:
  Part1 = Arduino Uno (Rev3)
  R1 = Resistor [tolerance=±5% resistance=100 package=THT]
  RP = PHOTOCELL [package=photocell]

nets:
  N1: Part1.A0, R1.Pin_0, RP.P$2
  N2: Part1.5V, RP.P$1
  N3: Part1.GND, R1.Pin_1
