# Fritzing sketch Night_Light (saved by Fritzing 0.9.2b)

parts:
  Part1 = Arduino Uno (Rev3)
  R1 = Resistor [tolerance=±5% resistance=100 package=THT]
  RP = PHOTOCELL [package=photocell]
  K1 = Relay [part_number=FRS1B-S package=THT]
  Lamp = Inductor [package="0805 [SMD]"]
  Vcc = Battery

nets:
  N1: Part1.A0, R1.Pin_0, RP.P$2
  N2: Part1.D13/SCK, K1.COIL2
  N3: Part1.GND, R1.Pin_1, K1.COIL1
  N4: Part1.5V, RP.P$1
  N5: K1.C1, K1.C2, Lamp.pin_0
  N6: K1.B, Vcc.-
  N7: Lamp.pin_1, Vcc.+
