# Fritzing sketch Project_1 (saved by Fritzing 0.9.2b)

parts:
  Part1 = Arduino Uno (Rev3)
  R1 = Resistor [tolerance=±5% resistance=100 package="1206 [SMD]"]
  D1 = LEDs [package=led10mm]

nets:
  N1: Part1.D2, R1.Pin_0
  N2: Part1.3V3, D1.A
  N3: R1.Pin_1, D1.C
