# Fritzing sketch Push_Button_Monitor (saved by Fritzing 0.9.2b)

parts:
  Part1 = Arduino Uno (Rev3)
  R1 = Resistor [tolerance=±5% resistance=100 package="1206 [SMD]"]
  D1 = LEDs [package=led10mm]
  S2 = SWITCH-MOMENTARY-2 [package=tactile-pth]
  R4 = Resistor [tolerance=±5% resistance=10k package="1206 [SMD]"]

nets:
  N1: Part1.GND, R4.Pin_0
  N2: Part1.D2, R1.Pin_0
  N3: Part1.D7, S2.2, R4.Pin_1
  N4: Part1.3V3, D1.A
  N5: Part1.5V, S2.1
  N6: R1.Pin_1, D1.C
