# Fritzing sketch Seven_Segment_Display (saved by Fritzing 0.9.2b)

parts:
  Part1 = Arduino Uno (Rev3)
  R1 = Resistor [tolerance=±5% resistance=100 package=THT]
  7_Segment = 7 Segment Display  # not connected

nets:
  N1: Part1.3V3, R1.Pin_0
