# Fritzing sketch Snapduino_Basics (saved by Fritzing 0.9.2b)

parts:
  S2 = Momentary Switch [package=ksa_sealed_tac_switch]
  D1 = Resistor [tolerance=±5% resistance=100 package=THT]
  LED1 = LED - 5mm [color="Red (633nm)" package="5 mm [THT]"]
  U1 = attiny85 [package=dip]

nets:
  RTS/green: S2.2, U1.Pin_1
  GND/black: S2.4, LED1.cathode, U1.Pin_4
  N1: D1.Pin_0, U1.Pin_3
  N2: D1.Pin_1, LED1.anode
  RX/yellow: U1.Pin_5
  TX/orange: U1.Pin_6
  5V/5V/red: U1.Pin_8

notes:
  Conected via FTDI Cable
